# Fritzing sketch breadboard (saved by Fritzing 0.9.3b)
breadboards: 6

parts:
  Microcontroller = IC, DIP package, 40 pins [chip_label="Atmega 162"]
  RESET = Pushbutton [package="[SMD]"]
  LED = LED - 3mm [color="Red (633nm)" package="3 mm [THT]"]
  VCC1 = Battery block 9V
  C3 = Capacitor [package=cap-pth-small]
  U1 = Voltage Regulator - 5V [package="TO220 [THT]"]
  Clock = Crystal [frequency="4 MHz" package=THT]
  UART_transceiver = IC, DIP package, 20 pins [chip_label=MAX233]
  C4 = Capacitor [package=cap-pth-large]
  UART = male pin header, 5 pins [form="♂ (male)"]
  CAN_controller = IC, DIP package, 18 pins [chip_label=MCP2515]
  C2 = Capacitor [package=cap-pth-large]
  CAN_transceiver = IC, DIP package, 8 pins [chip_label=MC2551]  # not connected
  Latch = IC, DIP package, 20 pins [chip_label=SN74ALS573C]
  C5 = Ceramic Capacitor [capacitance="100 nF" package="0603 [SMD, multilayer]"]
  ADC = IC, DIP package, 20 pins [chip_label=ADC0844CCN]

nets:
  GND: Microcontroller.pin1, Microcontroller.pin20, RESET.Pin_3, RESET.Pin_4, LED.cathode, LED.anode, VCC1.-, C3.2, U1.GND, UART_transceiver.pin6, C4.2, CAN_controller.pin9, C2.2, Latch.pin1, Latch.pin10, C5.1, ADC.pin7
  N1: Microcontroller.pin3, Microcontroller.pin9, RESET.Pin_1, RESET.Pin_2
  N2: Microcontroller.pin10, UART_transceiver.pin3
  N3: Microcontroller.pin11, UART_transceiver.pin2
  N4: Microcontroller.pin16, ADC.pin1, ADC.pin19
  N5: Microcontroller.pin18, Clock.pin_1
  N6: Microcontroller.pin19, Clock.pin_0
  N7: Microcontroller.pin30, Latch.pin11
  N8: Microcontroller.pin32, Latch.pin9
  N9: Microcontroller.pin33, Latch.pin8
  N10: Microcontroller.pin34, Latch.pin7
  N11: Microcontroller.pin35, Latch.pin6
  N12: Microcontroller.pin36, Latch.pin5
  N13: Microcontroller.pin37, Latch.pin4
  N14: Microcontroller.pin38, Latch.pin3
  N15: Microcontroller.pin39, Latch.pin2
  5V: Microcontroller.pin40, U1.output_voltage, UART_transceiver.pin7, C4.1, CAN_controller.pin18, C2.1
  N16: VCC1.+, C3.1, U1.input_voltage
  N17: UART_transceiver.pin4, UART.pin3
  N18: UART_transceiver.pin5, UART.pin4
  N19: UART_transceiver.pin10, UART_transceiver.pin16
  N20: UART_transceiver.pin11, UART_transceiver.pin15
  N21: UART_transceiver.pin12, UART_transceiver.pin17
  N22: Latch.pin20, C5.0, ADC.pin8

notes:
  TTK4255 - Byggern, This is the breadboard for Industrial Embedded., 1
